# Fritzing sketch Laser Engraver Circuit (saved by Fritzing 0.9.2b)
breadboards: 1

parts:
  Part1 = Arduino Uno (Rev3)
  MD09B1 = A4988 Stepper Motor Driver Carrier
  MD09B2 = A4988 Stepper Motor Driver Carrier
  M1 = Stepper Motor - Bipolar
  M2 = Stepper Motor - Bipolar
  Q1 = Basic FET P-Channel [package="TO220 [THT]"]
  LD1 = LD
  U1 = mystery part, 4 pins [chip_label="Voltage Regulator"]
  S1 = SWITCH-MOMENTARY-2 [package=tactile-switch-1101ne]
  S2 = SWITCH-MOMENTARY-2 [package=tactile-switch-1101ne]
  U2 = mystery part, 4 pins [chip_label="Laser Driver"]

nets:
  N1: Part1.D8, MD09B1.Enable
  N2: Part1.D9_PWM, S2.1
  N3: Part1.D10_PWM/SS, S1.1
  N4: Part1.D13/SCK, Q1.gate
  N5: Part1.GND, MD09B1.MS1, MD09B1.MS3, MD09B1.GROUND, MD09B2.MS1, MD09B2.MS3, MD09B2.GROUND, Q1.source
  N6: Part1.D2, MD09B2.STEP
  N7: Part1.D3_PWM, MD09B1.STEP
  N8: Part1.D5_PWM, MD09B2.DIR
  N9: Part1.D6_PWM, MD09B1.DIR
  VDD: Part1.5V, MD09B1.MS2, MD09B1.VDD, MD09B2.VDD, S1.2, S2.2
  N10: MD09B1.RESET, MD09B1.SLEEP
  N11: MD09B1.VMOT, MD09B2.VMOT, U1.pin1
  N12: MD09B1.OUT_2B, M1.A
  N13: MD09B1.OUT_2A, M1.C
  N14: MD09B1.OUT_1A, M1.B
  N15: MD09B1.OUT_1B, M1.D
  N16: MD09B2.RESET, MD09B2.SLEEP
  N17: MD09B2.OUT_2B, M2.A
  N18: MD09B2.OUT_2A, M2.C
  N19: MD09B2.OUT_1A, M2.B
  N20: MD09B2.OUT_1B, M2.D
  N21: Q1.drain, U1.pin2
  N22: LD1.cathode, U2.pin3
  N23: LD1.anode, U2.pin4
  N24: U1.pin3, U2.pin2
  N25: U1.pin4, U2.pin1

notes:
  12V 120W Power Supply
  Y and X axis limit switches, respectively
  LM2596 Voltage Regutlator set to 8.0V
  1.8A X-Drive Laser Driver
  2W M140 Laser Diode

custom parts:
  LD: A Generic Red Dot Laser Diode Module (~5mW)
